// Logisim project MIPS.circ as structural Verilog: 9 circuits, main circuit main
module main (
  input  in_1,
  input  in_2,
  input  in_3
);

  wire alu_16bits_1_negative, alu_16bits_1_zero, OUTr, We_RAM;
  wire [2:0] i_r_1_r1, i_r_1_r2, i_r_1_whrite;
  wire [3:0] i_r_1_sel;
  wire [4:0] program_cointer_1_saida, undriven;
  wire [15:0] alu_16bits_1_s, alu_16bits_2_s, bit_extender_1_out, registers_8x16_1_r1, registers_8x16_1_r2,
       rom_1_data;

  program_cointer program_cointer_1 (
    .Entrada(alu_16bits_1_s[4:0]), .Clock(in_1), .Clear(in_3), .Saida(program_cointer_1_saida));
  assign bit_extender_1_out = {{11{program_cointer_1_saida[4]}}, program_cointer_1_saida};  // Bit_Extender bit_extender_1
  ROM #(.addrWidth(5), .dataWidth(16)) rom_1 (.addr(program_cointer_1_saida), .data(rom_1_data));
  LED led_1 (.in(alu_16bits_1_zero));
  ALU_16bits alu_16bits_1 (
    .SEL(4'b0000), .A(16'h1), .B(bit_extender_1_out), .Zero(alu_16bits_1_zero), .S(alu_16bits_1_s),
    .Negative(alu_16bits_1_negative));
  LED led_2 (.in(alu_16bits_1_negative));
  I_R i_r_1 (.in_1(rom_1_data), .sel(i_r_1_sel), .whrite(i_r_1_whrite), .r1(i_r_1_r1), .r2(i_r_1_r2));
  Registers_8x16 registers_8x16_1 (
    .Le_r1(i_r_1_r1), .Le_r2(i_r_1_r2), .Whrite(in_2), .Entrada(alu_16bits_2_s),
    .We_registrador(i_r_1_whrite), .CLK(in_1), .r1(registers_8x16_1_r1), .r2(registers_8x16_1_r2));  // open: Reset
  ALU_16bits alu_16bits_2 (
    .SEL(i_r_1_sel), .A(registers_8x16_1_r1), .B(registers_8x16_1_r2), .S(alu_16bits_2_s));  // open: Zero, Negative
  RAM #(.addrWidth(5), .dataWidth(16)) ram_1 (
    .addr(undriven), .we(We_RAM), .oe(OUTr), .clk(in_1), .din(registers_8x16_1_r2));  // open: dout

  // Other names for the same wires on the sheet: Clear = in_3; CLK = in_1; We = in_2

  // Notes on the sheet:
  //   contents of rom_1 (hex, n*v repeats v):
  //   a1 b0
endmodule

module program_cointer (
  input  [4:0] Entrada,
  input  Clock,
  input  Clear,
  output [4:0] Saida
);

  D_Flip_Flop #(.trigger("falling")) d_ff_1 (
    .D(Entrada[4]), .clk(Clock), .Q(Saida[4]), .reset(Clear));  // open: Qn, preset
  D_Flip_Flop #(.trigger("falling")) d_ff_2 (
    .D(Entrada[3]), .clk(Clock), .Q(Saida[3]), .reset(Clear));  // open: Qn, preset
  D_Flip_Flop #(.trigger("falling")) d_ff_3 (
    .D(Entrada[2]), .clk(Clock), .Q(Saida[2]), .reset(Clear));  // open: Qn, preset
  D_Flip_Flop #(.trigger("falling")) d_ff_4 (
    .D(Entrada[1]), .clk(Clock), .Q(Saida[1]), .reset(Clear));  // open: Qn, preset
  D_Flip_Flop #(.trigger("falling")) d_ff_5 (
    .D(Entrada[0]), .clk(Clock), .Q(Saida[0]), .reset(Clear));  // open: Qn, preset
endmodule

module Registers_8x16 (
  input  [15:0] Entrada,
  input  Whrite,
  input  [2:0] Le_r1,
  input  [2:0] We_registrador,
  input  [2:0] Le_r2,
  input  Reset,
  input  CLK,
  output [15:0] r1,
  output [15:0] r2
);

  wire [15:0] register_1_q, register_2_q, register_3_q, register_4_q, register_5_q, register_6_q,
       register_7_q, register_8_q;
  wire [16:0] demultiplexer_1_out0, demultiplexer_1_out1, demultiplexer_1_out2, demultiplexer_1_out3,
       demultiplexer_1_out4, demultiplexer_1_out5, demultiplexer_1_out6, demultiplexer_1_out7;

  Demultiplexer #(.select(3), .width(17)) demultiplexer_1 (
    .out0(demultiplexer_1_out0), .out1(demultiplexer_1_out1), .out2(demultiplexer_1_out2),
    .out3(demultiplexer_1_out3), .out4(demultiplexer_1_out4), .out5(demultiplexer_1_out5),
    .out6(demultiplexer_1_out6), .out7(demultiplexer_1_out7), .in({Whrite, Entrada}), .sel(We_registrador));
  Register #(.width(16)) register_1 (
    .en(demultiplexer_1_out0[16]), .clk(CLK), .Q(register_1_q), .clr(Reset));  // open: D
  Register #(.width(16)) register_2 (
    .D(demultiplexer_1_out1[15:0]), .en(demultiplexer_1_out1[16]), .clk(CLK), .Q(register_2_q), .clr(Reset));
  Register #(.width(16)) register_3 (
    .D(demultiplexer_1_out2[15:0]), .en(demultiplexer_1_out2[16]), .clk(CLK), .Q(register_3_q), .clr(Reset));
  Register #(.width(16)) register_4 (
    .D(demultiplexer_1_out3[15:0]), .en(demultiplexer_1_out3[16]), .clk(CLK), .Q(register_4_q), .clr(Reset));
  Register #(.width(16)) register_5 (
    .D(demultiplexer_1_out4[15:0]), .en(demultiplexer_1_out4[16]), .clk(CLK), .Q(register_5_q), .clr(Reset));
  Register #(.width(16)) register_6 (
    .D(demultiplexer_1_out5[15:0]), .en(demultiplexer_1_out5[16]), .clk(CLK), .Q(register_6_q), .clr(Reset));
  Register #(.width(16)) register_7 (
    .D(demultiplexer_1_out6[15:0]), .en(demultiplexer_1_out6[16]), .clk(CLK), .Q(register_7_q), .clr(Reset));
  Register #(.width(16)) register_8 (
    .D(demultiplexer_1_out7[15:0]), .en(demultiplexer_1_out7[16]), .clk(CLK), .Q(register_8_q), .clr(Reset));
  Multiplexer #(.select(3), .width(16)) multiplexer_1 (
    .in0(register_1_q), .in1(register_2_q), .in2(register_3_q), .in3(register_4_q), .in4(register_5_q),
    .in5(register_6_q), .in6(register_7_q), .in7(register_8_q), .out(r1), .sel(Le_r1));
  Multiplexer #(.select(3), .width(16)) multiplexer_2 (
    .in0(register_1_q), .in1(register_2_q), .in2(register_3_q), .in3(register_4_q), .in4(register_5_q),
    .in5(register_6_q), .in6(register_7_q), .in7(register_8_q), .out(r2), .sel(Le_r2));
endmodule

module somador_1bit (
  input  A,
  input  B,
  input  Cin,
  output Cout,
  output Soma
);

  wire and_1_out, and_2_out, and_3_out, and_4_out, and_5_out, xnor_1_out, xor_1_out;

  and and_1 (and_1_out, A, B);
  and and_2 (and_2_out, A, Cin);
  and and_3 (and_3_out, B, Cin);
  xnor xnor_1 (xnor_1_out, A, B);
  xor xor_1 (xor_1_out, A, B);
  or or_1 (Cout, and_1_out, and_2_out, and_3_out);
  and and_4 (and_4_out, xnor_1_out, Cin);
  and and_5 (and_5_out, xor_1_out, ~Cin);  // AND_Gate
  or or_2 (Soma, and_4_out, and_5_out);
endmodule

module somador_subtrator_1bit (
  input  Cin,
  input  Sub,
  input  A,
  input  B,
  output S,
  output Cout
);

  wire xor_1_out;

  xor xor_1 (xor_1_out, Sub, B);
  somador_1bit somador_1bit_1 (.A(A), .B(xor_1_out), .Cin(Cin), .Cout(Cout), .Soma(S));
endmodule

module ALU_1bit (
  input  A,
  input  B,
  input  Cin,
  input  [3:0] sel,
  output Cout,
  output S
);

  wire and_1_out, nand_1_out, nor_1_out, or_1_out, somador_subtrator_1bit_1_s, xor_1_out;

  somador_subtrator_1bit somador_subtrator_1bit_1 (
    .A(A), .B(B), .Sub(sel[0]), .Cin(Cin), .Cout(Cout), .S(somador_subtrator_1bit_1_s));
  and and_1 (and_1_out, B, A);
  or or_1 (or_1_out, A, B);
  xor xor_1 (xor_1_out, A, B);
  nand nand_1 (nand_1_out, A, B);
  nor nor_1 (nor_1_out, A, B);
  Multiplexer #(.select(4)) multiplexer_1 (
    .in0(somador_subtrator_1bit_1_s), .in1(somador_subtrator_1bit_1_s), .in2(and_1_out), .in3(or_1_out),
    .in4(xor_1_out), .in5(nand_1_out), .in6(nor_1_out), .in7(somador_subtrator_1bit_1_s), .out(S), .sel(sel));  // open: in8, in9, in10, in11, in12, in13, in14, in15
endmodule

module ALU_16bits (
  input  [3:0] SEL,
  input  [15:0] A,
  input  [15:0] B,
  output [15:0] S,
  output Negative,
  output Zero
);

  wire alu_1bit_1_cout, alu_1bit_2_cout, alu_1bit_3_cout, alu_1bit_4_cout, alu_1bit_5_cout, alu_1bit_6_cout,
       alu_1bit_7_cout, alu_1bit_8_cout, alu_1bit_9_cout, alu_1bit_10_cout, alu_1bit_11_cout,
       alu_1bit_12_cout, alu_1bit_13_cout, alu_1bit_14_cout, alu_1bit_15_cout, and_1_out;
  wire [6:0] alu_1bit_9_s;
  wire [7:0] alu_1bit_1_s;

  ALU_1bit alu_1bit_1 (.sel(SEL), .A(A[0]), .B(B[0]), .Cin(SEL[0]), .Cout(alu_1bit_1_cout), .S(alu_1bit_1_s[0]));
  ALU_1bit alu_1bit_2 (
    .sel(SEL), .A(A[1]), .B(B[1]), .Cin(alu_1bit_1_cout), .Cout(alu_1bit_2_cout), .S(alu_1bit_1_s[1]));
  ALU_1bit alu_1bit_3 (
    .sel(SEL), .A(A[2]), .B(B[2]), .Cin(alu_1bit_2_cout), .Cout(alu_1bit_3_cout), .S(alu_1bit_1_s[2]));
  ALU_1bit alu_1bit_4 (
    .sel(SEL), .A(A[3]), .B(B[3]), .Cin(alu_1bit_3_cout), .Cout(alu_1bit_4_cout), .S(alu_1bit_1_s[3]));
  ALU_1bit alu_1bit_5 (
    .sel(SEL), .A(A[4]), .B(B[4]), .Cin(alu_1bit_4_cout), .Cout(alu_1bit_5_cout), .S(alu_1bit_1_s[4]));
  ALU_1bit alu_1bit_6 (
    .sel(SEL), .A(A[5]), .B(B[5]), .Cin(alu_1bit_5_cout), .Cout(alu_1bit_6_cout), .S(alu_1bit_1_s[5]));
  ALU_1bit alu_1bit_7 (
    .sel(SEL), .A(A[6]), .B(B[6]), .Cin(alu_1bit_6_cout), .Cout(alu_1bit_7_cout), .S(alu_1bit_1_s[6]));
  ALU_1bit alu_1bit_8 (
    .sel(SEL), .A(A[7]), .B(B[7]), .Cin(alu_1bit_7_cout), .Cout(alu_1bit_8_cout), .S(alu_1bit_1_s[7]));
  ALU_1bit alu_1bit_9 (
    .sel(SEL), .A(A[8]), .B(B[8]), .Cin(alu_1bit_8_cout), .Cout(alu_1bit_9_cout), .S(alu_1bit_9_s[0]));
  ALU_1bit alu_1bit_10 (
    .sel(SEL), .A(A[9]), .B(B[9]), .Cin(alu_1bit_9_cout), .Cout(alu_1bit_10_cout), .S(alu_1bit_9_s[1]));
  ALU_1bit alu_1bit_11 (
    .sel(SEL), .A(A[10]), .B(B[10]), .Cin(alu_1bit_10_cout), .Cout(alu_1bit_11_cout), .S(alu_1bit_9_s[2]));
  ALU_1bit alu_1bit_12 (
    .sel(SEL), .A(A[11]), .B(B[11]), .Cin(alu_1bit_11_cout), .Cout(alu_1bit_12_cout), .S(alu_1bit_9_s[3]));
  ALU_1bit alu_1bit_13 (
    .sel(SEL), .A(A[12]), .B(B[12]), .Cin(alu_1bit_12_cout), .Cout(alu_1bit_13_cout), .S(alu_1bit_9_s[4]));
  ALU_1bit alu_1bit_14 (
    .sel(SEL), .A(A[13]), .B(B[13]), .Cin(alu_1bit_13_cout), .Cout(alu_1bit_14_cout), .S(alu_1bit_9_s[5]));
  ALU_1bit alu_1bit_15 (
    .sel(SEL), .A(A[14]), .B(B[14]), .Cin(alu_1bit_14_cout), .Cout(alu_1bit_15_cout), .S(alu_1bit_9_s[6]));
  ALU_1bit alu_1bit_16 (.sel(SEL), .A(A[15]), .B(B[15]), .Cin(alu_1bit_15_cout), .S(Negative));  // open: Cout
  and and_1 (and_1_out, SEL[0], SEL[1], SEL[2], ~SEL[3]);  // AND_Gate
  Multiplexer #(.width(16)) multiplexer_1 (
    .in0({Negative, alu_1bit_9_s, alu_1bit_1_s}), .in1({{15{1'b0}}, Negative}), .out(S), .sel(and_1_out));
  nor nor_1 (Zero, alu_1bit_1_s[7], alu_1bit_1_s[0], alu_1bit_1_s[1], alu_1bit_1_s[2], alu_1bit_1_s[3], alu_1bit_1_s[4], alu_1bit_1_s[5], alu_1bit_1_s[6], alu_1bit_9_s[0], alu_1bit_9_s[1], alu_1bit_9_s[2], alu_1bit_9_s[3], alu_1bit_9_s[4], alu_1bit_9_s[5], alu_1bit_9_s[6], Negative);
endmodule

module Controller (
  input  [15:0] Entrada
);
endmodule

module I_R (
  input  [15:0] in_1,
  output [3:0] sel,
  output [2:0] whrite,
  output [2:0] r1,
  output [2:0] r2
);

  wire or_1_out;

  or or_1 (or_1_out, in_1[13], in_1[14], in_1[15]);
  Multiplexer #(.width(3)) multiplexer_1 (.in0(in_1[6:4]), .in1(in_1[12:10]), .out(whrite), .sel(or_1_out));
  Multiplexer #(.width(3)) multiplexer_2 (.in0(in_1[12:10]), .in1(in_1[9:7]), .out(r1), .sel(or_1_out));
  Multiplexer #(.width(3)) multiplexer_3 (.in0(in_1[9:7]), .in1(in_1[6:4]), .out(r2), .sel(or_1_out));

  assign sel = in_1[3:0];
endmodule
